// Logisim project sbc6526.circ as structural Verilog: 2 circuits, main circuit sbc6526
module sbc6526 (
  input  RDY,
  input  BE,
  output [15:0] out_3
);

  wire button_1_out, button_2_out, button_3_out, CIA_nirq, CIA_npc, CIAEXT_npc, CIAEXT_ocnt, CIAEXT_osp,
       clock_1_out, memdecoder_1_ncia, memdecoder_1_nciaext, memdecoder_1_nciares, memdecoder_1_oe,
       memdecoder_1_we, n6502_1_phi2, n6502_1_r_w, not_1_out, not_2_out, not_3_out, TERM, undriven_3;
  wire [7:0] CIA_pao, CIAEXT_pao, n6502_1_d_out, undriven, undriven_2, undriven_4;

  Clock clock_1 (.out(clock_1_out));
  _6502 u_6502_1 (
    .A_BUS(out_3), .D_OUT(n6502_1_d_out), .R_W(n6502_1_r_w), .PHI2(n6502_1_phi2), .PHI0(clock_1_out),
    .RDY(RDY), .BE(BE), .nRS(not_1_out), .nIRQ(not_2_out), .nNMI(not_3_out), .D_IN(n6502_1_d_out));  // open: AX_OUT, PHI1, SYNC
  not not_1 (not_1_out, button_3_out);
  not not_2 (not_2_out, button_1_out);
  Button button_1 (.out(button_1_out));
  not not_3 (not_3_out, button_2_out);
  Button button_2 (.out(button_2_out));
  Button button_3 (.out(button_3_out));
  TTY #(.asciiwidth(8), .cols(20)) tty_1 (.data(n6502_1_d_out[6:0]), .clk(TERM), .clr(button_3_out));  // open: we
  memDecoder memdecoder_1 (
    .A(out_3), .R_W(n6502_1_r_w), .PHI2(n6502_1_phi2), .OE(memdecoder_1_oe), .WE(memdecoder_1_we),
    .nCIA(memdecoder_1_ncia), .TERM(TERM), .nCIARES(memdecoder_1_nciares), .nCIAEXT(memdecoder_1_nciaext));
  _74hct6526 CIA (
    .oD(n6502_1_d_out), .nIRQ(CIA_nirq), .PAO(CIA_pao), .nPC(CIA_npc), .iD(n6502_1_d_out), .A(out_3),
    .iSP(CIAEXT_ocnt), .nFLAG(CIAEXT_npc), .PAI(undriven), .PBI(undriven_2), .nCS(memdecoder_1_ncia),
    .PHI2(n6502_1_phi2), .TOD(undriven_3), .RnW(n6502_1_r_w), .nRES(memdecoder_1_nciares), .CNT(CIAEXT_osp));  // open: oCNT, oSP, PBO
  _74hct6526 CIAEXT (
    .oD(n6502_1_d_out), .oCNT(CIAEXT_ocnt), .oSP(CIAEXT_osp), .PAO(CIAEXT_pao), .nPC(CIAEXT_npc),
    .iD(n6502_1_d_out), .A(out_3), .iSP(CIAEXT_osp), .nFLAG(CIA_npc), .PAI(undriven_4),
    .nCS(memdecoder_1_nciaext), .PHI2(n6502_1_phi2), .TOD(undriven_3), .RnW(n6502_1_r_w),
    .nRES(memdecoder_1_nciares), .CNT(CIAEXT_ocnt));  // open: nIRQ, PBO, PBI
  // RAM #(.addrWidth(16), .databus("bidir"), .trigger("high"), .\type ("nonvolatile")) ram_1: pin names not known; wires that end beside it: out_3, memdecoder_1_oe, memdecoder_1_we, 1'b1, n6502_1_d_out
  // Pins of 7 and 8 bits meet at n6502_1_d_out

  // Notes on the sheet:
  //   PHI0
  //   IRQ
  //   NMI
  //   addr
  //   PHI1
  //   PHI2
  //   R/W
  //   SYNC
  //   DATA
endmodule

module memDecoder (
  input  [15:0] A,
  input  R_W,
  input  PHI2,
  output OE,
  output WE,
  output nCIA,
  output TERM,
  output nCIARES,
  output nCIAEXT
);

  wire and_1_out, decoder_1_out2, decoder_2_out1, decoder_2_out3, not_2_out;
  wire [0:0] not_1_out;

  and and_1 (and_1_out, A[15], ~A[14]);  // AND_Gate
  not not_1 (not_1_out[0], PHI2);
  Decoder #(.enable("false"), .select(2)) decoder_1 (.out2(decoder_1_out2), .sel(A[15:14]));  // open: out0, out1, out3
  Decoder #(.select(3)) decoder_2 (
    .out1(decoder_2_out1), .out3(decoder_2_out3), .sel(A[13:11]), .en(and_1_out));  // open: out0, out2, out4, out5, out6, out7
  Decoder #(.select(2)) decoder_3 (
    .out0(WE), .out2(OE), .sel({R_W, not_1_out[0]}), .en(not_2_out));  // open: out1, out3
  nand nand_1 (nCIARES, WE, ~A[15], A[14], ~A[13], ~A[12]);  // NAND_Gate
  and u_TERM (TERM, WE, ~A[15], A[14], A[13], A[12]);  // AND_Gate
  not not_2 (not_2_out, decoder_1_out2);
  not not_3 (nCIA, decoder_2_out1);
  not not_4 (nCIAEXT, decoder_2_out3);
endmodule
