// Logisim project tem.circ as structural Verilog: 2 circuits, main circuit sbc6526
module sbc6526 (
);

  wire _1__PHI2, _1__RES, _1_OETAHI, _1_OETALO, _1_PHI2, _1_TADECREMENT, _1_TALOAD, _1_TALOADPULSE, _1_TAOUT,
       _1_TAOUTMODE, _1_TAPULSE, _1_TASTART, _1_TAUNDERFLOW, _1_WETAHI, d_ff_2_qn, d_ff_3_q, d_ff_4_qn,
       multiplexer_1_out, nor_1_out, nor_2_out, not_1_out, not_2_out, not_3_out, timer16_1_underflow,
       undriven;
  wire [7:0] _1_TALATCHHI, _1_TALATCHLO, D;

  not not_1 (not_1_out, nor_2_out);
  timer16 timer16_1 (
    .UNDERFLOW(timer16_1_underflow), .Q(D), .PULSE(_1_PHI2), .DECREMENT(_1_TADECREMENT),
    .FORCELOAD(_1_TALOADPULSE), .nRES(_1__RES), .LO(_1_TALATCHLO), .HI(_1_TALATCHHI), .nOELO(_1_OETALO),
    .nOEHI(_1_OETAHI));  // open: TIMER
  D_Flip_Flop d_ff_1 (.reset(not_1_out));  // open: clk, D, Q, Qn, preset
  buf and_1 (_1_TAUNDERFLOW, undriven);  // AND_Gate
  nor nor_1 (nor_1_out, _1_TASTART, _1_WETAHI, 1'b0);
  D_Flip_Flop d_ff_2 (.clk(_1_PHI2), .D(1'b0), .Q(_1_TAPULSE), .Qn(d_ff_2_qn), .preset(_1_TAUNDERFLOW));  // open: reset
  D_Flip_Flop d_ff_3 (.clk(_1_TASTART), .D(1'b1), .Q(d_ff_3_q), .reset(_1_PHI2));  // open: Qn, preset
  nor nor_2 (nor_2_out, _1_TAUNDERFLOW, _1_TALOAD, nor_1_out);
  D_Flip_Flop d_ff_4 (
    .clk(_1_TAPULSE), .D(d_ff_4_qn), .Qn(d_ff_4_qn), .preset(d_ff_3_q), .reset(not_2_out));  // open: Q
  not not_2 (not_2_out, _1__RES);
  D_Flip_Flop d_ff_5 (.clk(_1__PHI2), .D(1'b1), .Q(_1_TALOADPULSE), .reset(not_3_out));  // open: Qn, preset
  not not_3 (not_3_out, nor_2_out);
  not not_4 (_1_TAOUT, multiplexer_1_out);
  Multiplexer #(.enable("false")) multiplexer_1 (
    .in0(d_ff_2_qn), .in1(d_ff_4_qn), .out(multiplexer_1_out), .sel(_1_TAOUTMODE));
endmodule

module memDecoder (
  input  [15:0] A,
  input  R_W,
  input  PHI2,
  output OE,
  output WE,
  output nCIA,
  output TERM,
  output nCIARES,
  output nCIAEXT
);

  wire and_1_out, decoder_1_out2, decoder_2_out1, decoder_2_out3, decoder_2_out4, decoder_3_out1,
       decoder_3_out3, not_2_out;
  wire [0:0] not_1_out;

  and and_1 (and_1_out, A[15], ~A[14]);  // AND_Gate
  not not_1 (not_1_out[0], PHI2);
  Decoder #(.enable("false"), .select(2)) decoder_1 (.out2(decoder_1_out2), .sel(A[15:14]));  // open: out0, out1, out3
  Decoder #(.select(3)) decoder_2 (
    .out1(decoder_2_out1), .out3(decoder_2_out3), .out4(decoder_2_out4), .sel(A[13:11]), .en(and_1_out));  // open: out0, out2, out5, out6, out7
  Decoder #(.select(2)) decoder_3 (
    .out0(WE), .out1(decoder_3_out1), .out2(OE), .out3(decoder_3_out3), .sel({R_W, not_1_out[0]}),
    .en(not_2_out));
  not not_2 (not_2_out, decoder_1_out2);
  not not_3 (nCIA, decoder_2_out1);
  not not_4 (nCIAEXT, decoder_2_out3);
  and and_2 (TERM, ~A[0], PHI2, decoder_2_out4);  // AND_Gate
  nand nand_1 (nCIARES, A[0], decoder_2_out4);
endmodule
